// Logisim project Lab.circ as structural Verilog
module HalfAdder (
  input  a,
  input  b,
  output c,
  output s
);

  wire and_2_out, and_3_out, not_1_out, not_2_out;

  and and_1 (c, a, b);
  not not_1 (not_1_out, a);
  not not_2 (not_2_out, b);
  and and_2 (and_2_out, not_1_out, b);
  and and_3 (and_3_out, a, not_2_out);
  or or_1 (s, and_2_out, and_3_out);
endmodule

module FullAdder (
  input  Cin,
  input  a,
  input  b,
  output Cout,
  output s
);

  wire and_1_out, and_2_out, and_3_out, and_4_out, and_5_out, and_6_out, and_7_out, and_8_out, and_9_out,
       and_10_out, and_11_out, not_1_out, not_2_out, not_3_out, not_4_out, not_5_out, not_6_out, or_1_out,
       or_3_out, or_4_out;

  and and_1 (and_1_out, a, b);
  and and_2 (and_2_out, Cin, b);
  not not_1 (not_1_out, Cin);
  not not_2 (not_2_out, a);
  not not_3 (not_3_out, Cin);
  not not_4 (not_4_out, a);
  or or_1 (or_1_out, and_1_out, and_2_out);
  and and_3 (and_3_out, Cin, a);
  and and_4 (and_4_out, not_1_out, not_2_out);
  and and_5 (and_5_out, not_3_out, a);
  not not_5 (not_5_out, b);
  and and_6 (and_6_out, Cin, not_4_out);
  not not_6 (not_6_out, b);
  and and_7 (and_7_out, Cin, a);
  or or_2 (Cout, or_1_out, and_3_out);
  and and_8 (and_8_out, and_4_out, b);
  and and_9 (and_9_out, and_5_out, not_5_out);
  and and_10 (and_10_out, and_6_out, not_6_out);
  and and_11 (and_11_out, and_7_out, b);
  or or_3 (or_3_out, and_8_out, and_9_out);
  or or_4 (or_4_out, and_10_out, and_11_out);
  or or_5 (s, or_3_out, or_4_out);
endmodule
